// Logisim project Main.circ as structural Verilog: 6 circuits, main circuit Main
module Main (
  input  in_1,
  input  in_2
);

  wire button_1_out, button_2_out, button_3_out, stage1_1_outstream;
  wire [2:0] stage4_1_ss0, stage5_1_ss0;
  wire [3:0] stage4_1_m0, stage4_1_mm0, stage4_1_s0, stage5_1_m0, stage5_1_mm0, stage5_1_s0;

  Button button_1 (.out(button_1_out));
  Button button_2 (.out(button_2_out));
  Button button_3 (.out(button_3_out));
  Stage1 stage1_1 (.On_Off(button_1_out), .Outstream(stage1_1_outstream));
  Stage4 stage4_1 (
    .On_Off(stage1_1_outstream), .Reset(button_3_out), .S0(stage4_1_s0[0]), .S1(stage4_1_s0[1]),
    .S2(stage4_1_s0[2]), .S3(stage4_1_s0[3]), .SS0(stage4_1_ss0[0]), .SS1(stage4_1_ss0[1]),
    .SS2(stage4_1_ss0[2]), .M0(stage4_1_m0[0]), .M1(stage4_1_m0[1]), .M2(stage4_1_m0[2]),
    .M3(stage4_1_m0[3]), .MM0(stage4_1_mm0[0]), .MM1(stage4_1_mm0[1]), .MM2(stage4_1_mm0[2]),
    .MM3(stage4_1_mm0[3]));
  Stage5 stage5_1 (
    .Split(button_2_out), .On_Off(stage1_1_outstream), .Reset(button_3_out), .S0(stage5_1_s0[0]),
    .S1(stage5_1_s0[1]), .S2(stage5_1_s0[2]), .S3(stage5_1_s0[3]), .SS0(stage5_1_ss0[0]),
    .SS1(stage5_1_ss0[1]), .SS2(stage5_1_ss0[2]), .M0(stage5_1_m0[0]), .M1(stage5_1_m0[1]),
    .M2(stage5_1_m0[2]), .M3(stage5_1_m0[3]), .MM0(stage5_1_mm0[0]), .MM1(stage5_1_mm0[1]),
    .MM2(stage5_1_mm0[2]), .MM3(stage5_1_mm0[3]));
  LED led_1 (.in(stage1_1_outstream));
  Hex_Digit_Display hex_digit_display_1 (.value(stage4_1_mm0));  // open: dp
  Hex_Digit_Display hex_digit_display_2 (.value(stage4_1_m0));  // open: dp
  Hex_Digit_Display hex_digit_display_3 (.value({in_1, stage4_1_ss0}));  // open: dp
  Hex_Digit_Display hex_digit_display_4 (.value(stage4_1_s0));  // open: dp
  Hex_Digit_Display hex_digit_display_5 (.value(stage5_1_mm0));  // open: dp
  Hex_Digit_Display hex_digit_display_6 (.value(stage5_1_m0));  // open: dp
  Hex_Digit_Display hex_digit_display_7 (.value({in_2, stage5_1_ss0}));  // open: dp
  Hex_Digit_Display hex_digit_display_8 (.value(stage5_1_s0));  // open: dp

  // Notes on the sheet:
  //   Start / Stop
  //   Stopwatch Interface
  //   Split
  //   Reset
  //   Clock Started
  //   Minutes
  //   Elapsed Time
  //   :
  //   Seconds
  //   Minutes
  //   Split Time
  //   :
  //   Seconds
endmodule

module Stage1 (
  input  On_Off,
  output Outstream
);

  T_Flip_Flop t_ff_1 (.T(1'b1), .clk(On_Off), .Q(Outstream));  // open: Qn, reset, preset
endmodule

module Stage2 (
  input  On_Off,
  input  Reset,
  output Reset_Button,
  output Main_Clock,
  output S0,
  output S1,
  output S2,
  output S3,
  output C1
);

  wire and_1_out, and_3_out, and_4_out, and_5_out, j_k_ff_1_q, j_k_ff_2_q, j_k_ff_3_q, j_k_ff_4_q, or_1_out;

  Clock M_clock (.out(Main_Clock));
  J_K_Flip_Flop j_k_ff_1 (
    .J(On_Off), .K(On_Off), .clk(Main_Clock), .Q(j_k_ff_1_q), .reset(or_1_out));  // open: Qn, preset
  and and_1 (and_1_out, On_Off, j_k_ff_1_q);
  D_Flip_Flop d_ff_1 (.D(j_k_ff_1_q), .clk(Main_Clock), .Q(S0), .reset(Reset));  // open: Qn, preset
  J_K_Flip_Flop j_k_ff_2 (
    .J(and_1_out), .K(and_1_out), .clk(Main_Clock), .Q(j_k_ff_2_q), .reset(or_1_out));  // open: Qn, preset
  and and_2 (C1, S0, S3);
  and and_3 (and_3_out, and_1_out, j_k_ff_2_q);
  D_Flip_Flop d_ff_2 (.D(j_k_ff_2_q), .clk(Main_Clock), .Q(S1), .reset(Reset));  // open: Qn, preset
  J_K_Flip_Flop j_k_ff_3 (
    .J(and_3_out), .K(and_3_out), .clk(Main_Clock), .Q(j_k_ff_3_q), .reset(or_1_out));  // open: Qn, preset
  Hex_Digit_Display hex_digit_display_1 (.value({S3, S2, S1, S0}));  // open: dp
  and and_4 (and_4_out, and_3_out, j_k_ff_3_q);
  D_Flip_Flop d_ff_3 (.D(j_k_ff_3_q), .clk(Main_Clock), .Q(S2), .reset(Reset));  // open: Qn, preset
  J_K_Flip_Flop j_k_ff_4 (
    .J(and_4_out), .K(and_4_out), .clk(Main_Clock), .Q(j_k_ff_4_q), .reset(or_1_out));  // open: Qn, preset
  and and_5 (and_5_out, j_k_ff_2_q, j_k_ff_4_q);
  or or_1 (or_1_out, and_5_out, Reset);
  D_Flip_Flop d_ff_4 (.D(j_k_ff_4_q), .clk(Main_Clock), .Q(S3), .reset(Reset));  // open: Qn, preset

  assign Reset_Button = Reset;
endmodule

module Stage3 (
  input  On_Off,
  input  Reset,
  input  Zero,
  output Reset_Button,
  output Main_Clock,
  output S0,
  output S1,
  output S2,
  output S3,
  output C1,
  output SS0,
  output SS1,
  output SS2,
  output C2
);

  wire and_2_out, and_3_out, j_k_ff_1_q, j_k_ff_2_q, j_k_ff_3_q, or_1_out;

  J_K_Flip_Flop j_k_ff_1 (.J(1'b1), .K(1'b1), .clk(C1), .Q(j_k_ff_1_q), .reset(or_1_out));  // open: Qn, preset
  Hex_Digit_Display hex_digit_display_1 (.value({Zero, SS2, SS1, SS0}));  // open: dp
  D_Flip_Flop d_ff_1 (.D(j_k_ff_1_q), .clk(Main_Clock), .Q(SS0), .reset(Reset_Button));  // open: Qn, preset
  and and_1 (C2, SS0, SS2);
  Stage2 stage2_1 (
    .On_Off(On_Off), .Reset(Reset), .Reset_Button(Reset_Button), .Main_Clock(Main_Clock), .S0(S0), .S1(S1),
    .S2(S2), .S3(S3), .C1(C1));
  J_K_Flip_Flop j_k_ff_2 (
    .J(j_k_ff_1_q), .K(j_k_ff_1_q), .clk(C1), .Q(j_k_ff_2_q), .reset(or_1_out));  // open: Qn, preset
  and and_2 (and_2_out, j_k_ff_1_q, j_k_ff_2_q);
  J_K_Flip_Flop j_k_ff_3 (
    .J(and_2_out), .K(and_2_out), .clk(C1), .Q(j_k_ff_3_q), .reset(or_1_out));  // open: Qn, preset
  D_Flip_Flop d_ff_2 (.D(j_k_ff_2_q), .clk(Main_Clock), .Q(SS1), .reset(Reset_Button));  // open: Qn, preset
  or or_1 (or_1_out, and_3_out, Reset_Button);
  D_Flip_Flop d_ff_3 (.D(j_k_ff_3_q), .clk(Main_Clock), .Q(SS2), .reset(Reset_Button));  // open: Qn, preset
  and and_3 (and_3_out, j_k_ff_2_q, j_k_ff_3_q);
endmodule

module Stage4 (
  input  On_Off,
  input  Reset,
  output S0,
  output S1,
  output S2,
  output S3,
  output SS0,
  output SS1,
  output SS2,
  output M0,
  output M1,
  output M2,
  output M3,
  output MM0,
  output MM1,
  output MM2,
  output MM3
);

  wire and_1_out, and_2_out, and_3_out, and_4_out, and_5_out, and_6_out, and_7_out, or_1_out, or_2_out,
       stage3_1_c1, stage3_1_c2, stage3_1_main_clock, stage3_1_reset_button, t_ff_1_q, t_ff_2_q, t_ff_3_q,
       t_ff_4_q, t_ff_5_q, t_ff_6_q, t_ff_7_q, t_ff_8_q;

  Hex_Digit_Display hex_digit_display_1 (.value({MM3, MM2, MM1, MM0}));  // open: dp
  Hex_Digit_Display hex_digit_display_2 (.value({M3, M2, M1, M0}));  // open: dp
  Stage3 stage3_1 (
    .On_Off(On_Off), .Reset(Reset), .Reset_Button(stage3_1_reset_button), .Main_Clock(stage3_1_main_clock),
    .S0(S0), .S1(S1), .S2(S2), .S3(S3), .C1(stage3_1_c1), .SS0(SS0), .SS1(SS1), .SS2(SS2), .C2(stage3_1_c2));  // open: Zero
  and and_1 (and_1_out, stage3_1_c2, stage3_1_c1);
  T_Flip_Flop t_ff_1 (.T(1'b1), .clk(and_1_out), .Q(t_ff_1_q), .reset(or_1_out));  // open: Qn, preset
  T_Flip_Flop t_ff_2 (.T(1'b1), .clk(or_1_out), .Q(t_ff_2_q), .reset(or_2_out));  // open: Qn, preset
  D_Flip_Flop d_ff_1 (
    .D(t_ff_1_q), .clk(stage3_1_main_clock), .Q(M0), .reset(stage3_1_reset_button));  // open: Qn, preset
  D_Flip_Flop d_ff_2 (
    .D(t_ff_2_q), .clk(stage3_1_main_clock), .Q(MM0), .reset(stage3_1_reset_button));  // open: Qn, preset
  T_Flip_Flop t_ff_3 (.T(t_ff_1_q), .clk(and_1_out), .Q(t_ff_3_q), .reset(or_1_out));  // open: Qn, preset
  T_Flip_Flop t_ff_4 (.T(t_ff_2_q), .clk(or_1_out), .Q(t_ff_4_q), .reset(or_2_out));  // open: Qn, preset
  and and_2 (and_2_out, t_ff_1_q, t_ff_3_q);
  D_Flip_Flop d_ff_3 (
    .D(t_ff_3_q), .clk(stage3_1_main_clock), .Q(M1), .reset(stage3_1_reset_button));  // open: Qn, preset
  and and_3 (and_3_out, t_ff_2_q, t_ff_4_q);
  D_Flip_Flop d_ff_4 (
    .D(t_ff_4_q), .clk(stage3_1_main_clock), .Q(MM1), .reset(stage3_1_reset_button));  // open: Qn, preset
  T_Flip_Flop t_ff_5 (.T(and_2_out), .clk(and_1_out), .Q(t_ff_5_q), .reset(or_1_out));  // open: Qn, preset
  T_Flip_Flop t_ff_6 (.T(and_3_out), .clk(or_1_out), .Q(t_ff_6_q), .reset(or_2_out));  // open: Qn, preset
  and and_4 (and_4_out, and_2_out, t_ff_5_q);
  D_Flip_Flop d_ff_5 (
    .D(t_ff_5_q), .clk(stage3_1_main_clock), .Q(M2), .reset(stage3_1_reset_button));  // open: Qn, preset
  and and_5 (and_5_out, and_3_out, t_ff_6_q);
  D_Flip_Flop d_ff_6 (
    .D(t_ff_6_q), .clk(stage3_1_main_clock), .Q(MM2), .reset(stage3_1_reset_button));  // open: Qn, preset
  T_Flip_Flop t_ff_7 (.T(and_4_out), .clk(and_1_out), .Q(t_ff_7_q), .reset(or_1_out));  // open: Qn, preset
  T_Flip_Flop t_ff_8 (.T(and_5_out), .clk(or_1_out), .Q(t_ff_8_q), .reset(or_2_out));  // open: Qn, preset
  and and_6 (and_6_out, t_ff_3_q, t_ff_7_q);
  or or_1 (or_1_out, and_6_out, stage3_1_reset_button);
  D_Flip_Flop d_ff_7 (
    .D(t_ff_7_q), .clk(stage3_1_main_clock), .Q(M3), .reset(stage3_1_reset_button));  // open: Qn, preset
  and and_7 (and_7_out, t_ff_4_q, t_ff_8_q);
  or or_2 (or_2_out, and_7_out, stage3_1_reset_button);
  D_Flip_Flop d_ff_8 (
    .D(t_ff_8_q), .clk(stage3_1_main_clock), .Q(MM3), .reset(stage3_1_reset_button));  // open: Qn, preset
endmodule

module Stage5 (
  input  Split,
  input  On_Off,
  input  Reset,
  output S0,
  output S1,
  output S2,
  output S3,
  output SS0,
  output SS1,
  output SS2,
  output M0,
  output M1,
  output M2,
  output M3,
  output MM0,
  output MM1,
  output MM2,
  output MM3
);

  wire stage4_1_m0, stage4_1_m1, stage4_1_m2, stage4_1_m3, stage4_1_mm0, stage4_1_mm1, stage4_1_mm2,
       stage4_1_mm3, stage4_1_s0, stage4_1_s1, stage4_1_s2, stage4_1_s3, stage4_1_ss0, stage4_1_ss1,
       stage4_1_ss2;

  Stage4 stage4_1 (
    .On_Off(On_Off), .Reset(Reset), .S0(stage4_1_s0), .S1(stage4_1_s1), .S2(stage4_1_s2), .S3(stage4_1_s3),
    .SS0(stage4_1_ss0), .SS1(stage4_1_ss1), .SS2(stage4_1_ss2), .M0(stage4_1_m0), .M1(stage4_1_m1),
    .M2(stage4_1_m2), .M3(stage4_1_m3), .MM0(stage4_1_mm0), .MM1(stage4_1_mm1), .MM2(stage4_1_mm2),
    .MM3(stage4_1_mm3));
  D_Flip_Flop d_ff_1 (.D(stage4_1_s0), .clk(Split), .Q(S0), .reset(Reset));  // open: Qn, preset
  D_Flip_Flop d_ff_2 (.D(stage4_1_s1), .clk(Split), .Q(S1), .reset(Reset));  // open: Qn, preset
  D_Flip_Flop d_ff_3 (.D(stage4_1_s2), .clk(Split), .Q(S2), .reset(Reset));  // open: Qn, preset
  D_Flip_Flop d_ff_4 (.D(stage4_1_s3), .clk(Split), .Q(S3), .reset(Reset));  // open: Qn, preset
  D_Flip_Flop d_ff_5 (.D(stage4_1_ss0), .clk(Split), .Q(SS0), .reset(Reset));  // open: Qn, preset
  D_Flip_Flop d_ff_6 (.D(stage4_1_ss1), .clk(Split), .Q(SS1), .reset(Reset));  // open: Qn, preset
  D_Flip_Flop d_ff_7 (.D(stage4_1_ss2), .clk(Split), .Q(SS2), .reset(Reset));  // open: Qn, preset
  D_Flip_Flop d_ff_8 (.D(stage4_1_m0), .clk(Split), .Q(M0), .reset(Reset));  // open: Qn, preset
  D_Flip_Flop d_ff_9 (.D(stage4_1_m1), .clk(Split), .Q(M1), .reset(Reset));  // open: Qn, preset
  D_Flip_Flop d_ff_10 (.D(stage4_1_m2), .clk(Split), .Q(M2), .reset(Reset));  // open: Qn, preset
  D_Flip_Flop d_ff_11 (.D(stage4_1_m3), .clk(Split), .Q(M3), .reset(Reset));  // open: Qn, preset
  D_Flip_Flop d_ff_12 (.D(stage4_1_mm0), .clk(Split), .Q(MM0), .reset(Reset));  // open: Qn, preset
  D_Flip_Flop d_ff_13 (.D(stage4_1_mm1), .clk(Split), .Q(MM1), .reset(Reset));  // open: Qn, preset
  D_Flip_Flop d_ff_14 (.D(stage4_1_mm2), .clk(Split), .Q(MM2), .reset(Reset));  // open: Qn, preset
  D_Flip_Flop d_ff_15 (.D(stage4_1_mm3), .clk(Split), .Q(MM3), .reset(Reset));  // open: Qn, preset
endmodule
