// Logisim project Stage.1.circ as structural Verilog: 1 circuit, main circuit main
module main (
  input  On_Off,
  output Outstream
);

  T_Flip_Flop t_ff_1 (.T(1'b1), .clk(On_Off), .Q(Outstream));  // open: Qn, reset, preset
endmodule
