// Logisim project Stage.2.circ as structural Verilog: 1 circuit, main circuit main
module main (
  input  On_Off,
  input  Reset,
  output Reset_Button,
  output Main_Clock,
  output S0,
  output S1,
  output S2,
  output S3,
  output C1
);

  wire and_1_out, and_3_out, and_4_out, and_5_out, j_k_ff_1_q, j_k_ff_2_q, j_k_ff_3_q, j_k_ff_4_q, or_1_out;

  Clock M_clock (.out(Main_Clock));
  J_K_Flip_Flop j_k_ff_1 (
    .J(On_Off), .K(On_Off), .clk(Main_Clock), .Q(j_k_ff_1_q), .reset(or_1_out));  // open: Qn, preset
  and and_1 (and_1_out, On_Off, j_k_ff_1_q);
  D_Flip_Flop d_ff_1 (.D(j_k_ff_1_q), .clk(Main_Clock), .Q(S0), .reset(Reset));  // open: Qn, preset
  J_K_Flip_Flop j_k_ff_2 (
    .J(and_1_out), .K(and_1_out), .clk(Main_Clock), .Q(j_k_ff_2_q), .reset(or_1_out));  // open: Qn, preset
  and and_2 (C1, S0, S3);
  and and_3 (and_3_out, and_1_out, j_k_ff_2_q);
  D_Flip_Flop d_ff_2 (.D(j_k_ff_2_q), .clk(Main_Clock), .Q(S1), .reset(Reset));  // open: Qn, preset
  J_K_Flip_Flop j_k_ff_3 (
    .J(and_3_out), .K(and_3_out), .clk(Main_Clock), .Q(j_k_ff_3_q), .reset(or_1_out));  // open: Qn, preset
  Hex_Digit_Display hex_digit_display_1 (.value({S3, S2, S1, S0}));  // open: dp
  and and_4 (and_4_out, and_3_out, j_k_ff_3_q);
  D_Flip_Flop d_ff_3 (.D(j_k_ff_3_q), .clk(Main_Clock), .Q(S2), .reset(Reset));  // open: Qn, preset
  J_K_Flip_Flop j_k_ff_4 (
    .J(and_4_out), .K(and_4_out), .clk(Main_Clock), .Q(j_k_ff_4_q), .reset(or_1_out));  // open: Qn, preset
  and and_5 (and_5_out, j_k_ff_2_q, j_k_ff_4_q);
  or or_1 (or_1_out, and_5_out, Reset);
  D_Flip_Flop d_ff_4 (.D(j_k_ff_4_q), .clk(Main_Clock), .Q(S3), .reset(Reset));  // open: Qn, preset

  assign Reset_Button = Reset;
endmodule
