// Logisim project Stage.3.circ as structural Verilog: 1 circuit, main circuit main
module main (
  input  On_Off,
  input  Reset,
  input  Zero,
  output Reset_Button,
  output Main_Clock,
  output S0,
  output S1,
  output S2,
  output S3,
  output C1,
  output SS0,
  output SS1,
  output SS2,
  output C2
);

  wire and_2_out, and_3_out, j_k_ff_1_q, j_k_ff_2_q, j_k_ff_3_q, or_1_out;

  J_K_Flip_Flop j_k_ff_1 (.J(1'b1), .K(1'b1), .clk(C1), .Q(j_k_ff_1_q), .reset(or_1_out));  // open: Qn, preset
  Hex_Digit_Display hex_digit_display_1 (.value({Zero, SS2, SS1, SS0}));  // open: dp
  D_Flip_Flop d_ff_1 (.D(j_k_ff_1_q), .clk(Main_Clock), .Q(SS0), .reset(Reset_Button));  // open: Qn, preset
  and and_1 (C2, SS0, SS2);
  J_K_Flip_Flop j_k_ff_2 (
    .J(j_k_ff_1_q), .K(j_k_ff_1_q), .clk(C1), .Q(j_k_ff_2_q), .reset(or_1_out));  // open: Qn, preset
  and and_2 (and_2_out, j_k_ff_1_q, j_k_ff_2_q);
  J_K_Flip_Flop j_k_ff_3 (
    .J(and_2_out), .K(and_2_out), .clk(C1), .Q(j_k_ff_3_q), .reset(or_1_out));  // open: Qn, preset
  D_Flip_Flop d_ff_2 (.D(j_k_ff_2_q), .clk(Main_Clock), .Q(SS1), .reset(Reset_Button));  // open: Qn, preset
  or or_1 (or_1_out, and_3_out, Reset_Button);
  D_Flip_Flop d_ff_3 (.D(j_k_ff_3_q), .clk(Main_Clock), .Q(SS2), .reset(Reset_Button));  // open: Qn, preset
  and and_3 (and_3_out, j_k_ff_2_q, j_k_ff_3_q);

  // Notes on the sheet:
  //   Stage 2
endmodule
