// Logisim project Stage.4.circ as structural Verilog: 1 circuit, main circuit main
module main (
  input  On_Off,
  input  Reset,
  output S0,
  output S1,
  output S2,
  output S3,
  output SS0,
  output SS1,
  output SS2,
  output M0,
  output M1,
  output M2,
  output M3,
  output MM0,
  output MM1,
  output MM2,
  output MM3
);

  wire and_1_out, and_2_out, and_3_out, and_4_out, and_5_out, and_6_out, and_7_out, or_1_out, or_2_out,
       t_ff_1_q, t_ff_2_q, t_ff_3_q, t_ff_4_q, t_ff_5_q, t_ff_6_q, t_ff_7_q, t_ff_8_q, undriven, undriven_2,
       undriven_3, undriven_4;

  Hex_Digit_Display hex_digit_display_1 (.value({MM3, MM2, MM1, MM0}));  // open: dp
  Hex_Digit_Display hex_digit_display_2 (.value({M3, M2, M1, M0}));  // open: dp
  and and_1 (and_1_out, undriven_3, undriven_2);
  T_Flip_Flop t_ff_1 (.T(1'b1), .clk(and_1_out), .Q(t_ff_1_q), .reset(or_1_out));  // open: Qn, preset
  T_Flip_Flop t_ff_2 (.T(1'b1), .clk(or_1_out), .Q(t_ff_2_q), .reset(or_2_out));  // open: Qn, preset
  D_Flip_Flop d_ff_1 (.D(t_ff_1_q), .clk(undriven_4), .Q(M0), .reset(undriven));  // open: Qn, preset
  D_Flip_Flop d_ff_2 (.D(t_ff_2_q), .clk(undriven_4), .Q(MM0), .reset(undriven));  // open: Qn, preset
  T_Flip_Flop t_ff_3 (.T(t_ff_1_q), .clk(and_1_out), .Q(t_ff_3_q), .reset(or_1_out));  // open: Qn, preset
  T_Flip_Flop t_ff_4 (.T(t_ff_2_q), .clk(or_1_out), .Q(t_ff_4_q), .reset(or_2_out));  // open: Qn, preset
  and and_2 (and_2_out, t_ff_1_q, t_ff_3_q);
  D_Flip_Flop d_ff_3 (.D(t_ff_3_q), .clk(undriven_4), .Q(M1), .reset(undriven));  // open: Qn, preset
  and and_3 (and_3_out, t_ff_2_q, t_ff_4_q);
  D_Flip_Flop d_ff_4 (.D(t_ff_4_q), .clk(undriven_4), .Q(MM1), .reset(undriven));  // open: Qn, preset
  T_Flip_Flop t_ff_5 (.T(and_2_out), .clk(and_1_out), .Q(t_ff_5_q), .reset(or_1_out));  // open: Qn, preset
  T_Flip_Flop t_ff_6 (.T(and_3_out), .clk(or_1_out), .Q(t_ff_6_q), .reset(or_2_out));  // open: Qn, preset
  and and_4 (and_4_out, and_2_out, t_ff_5_q);
  D_Flip_Flop d_ff_5 (.D(t_ff_5_q), .clk(undriven_4), .Q(M2), .reset(undriven));  // open: Qn, preset
  and and_5 (and_5_out, and_3_out, t_ff_6_q);
  D_Flip_Flop d_ff_6 (.D(t_ff_6_q), .clk(undriven_4), .Q(MM2), .reset(undriven));  // open: Qn, preset
  T_Flip_Flop t_ff_7 (.T(and_4_out), .clk(and_1_out), .Q(t_ff_7_q), .reset(or_1_out));  // open: Qn, preset
  T_Flip_Flop t_ff_8 (.T(and_5_out), .clk(or_1_out), .Q(t_ff_8_q), .reset(or_2_out));  // open: Qn, preset
  and and_6 (and_6_out, t_ff_3_q, t_ff_7_q);
  or or_1 (or_1_out, and_6_out, undriven);
  D_Flip_Flop d_ff_7 (.D(t_ff_7_q), .clk(undriven_4), .Q(M3), .reset(undriven));  // open: Qn, preset
  and and_7 (and_7_out, t_ff_4_q, t_ff_8_q);
  or or_2 (or_2_out, and_7_out, undriven);
  D_Flip_Flop d_ff_8 (.D(t_ff_8_q), .clk(undriven_4), .Q(MM3), .reset(undriven));  // open: Qn, preset

  // Notes on the sheet:
  //   Stage 3
endmodule
