// Logisim project Stage.5.circ as structural Verilog: 1 circuit, main circuit main
module main (
  input  Split,
  input  On_Off,
  input  Reset,
  output S0,
  output S1,
  output S2,
  output S3,
  output SS0,
  output SS1,
  output SS2,
  output M0,
  output M1,
  output M2,
  output M3,
  output MM0,
  output MM1,
  output MM2,
  output MM3
);

  wire undriven, undriven_2, undriven_3, undriven_4, undriven_5, undriven_6, undriven_7, undriven_8,
       undriven_9, undriven_10, undriven_11, undriven_12, undriven_13, undriven_14, undriven_15;

  D_Flip_Flop d_ff_1 (.D(undriven), .clk(Split), .Q(S0), .reset(Reset));  // open: Qn, preset
  D_Flip_Flop d_ff_2 (.D(undriven_10), .clk(Split), .Q(S1), .reset(Reset));  // open: Qn, preset
  D_Flip_Flop d_ff_3 (.D(undriven_11), .clk(Split), .Q(S2), .reset(Reset));  // open: Qn, preset
  D_Flip_Flop d_ff_4 (.D(undriven_12), .clk(Split), .Q(S3), .reset(Reset));  // open: Qn, preset
  D_Flip_Flop d_ff_5 (.D(undriven_13), .clk(Split), .Q(SS0), .reset(Reset));  // open: Qn, preset
  D_Flip_Flop d_ff_6 (.D(undriven_14), .clk(Split), .Q(SS1), .reset(Reset));  // open: Qn, preset
  D_Flip_Flop d_ff_7 (.D(undriven_15), .clk(Split), .Q(SS2), .reset(Reset));  // open: Qn, preset
  D_Flip_Flop d_ff_8 (.D(undriven_2), .clk(Split), .Q(M0), .reset(Reset));  // open: Qn, preset
  D_Flip_Flop d_ff_9 (.D(undriven_3), .clk(Split), .Q(M1), .reset(Reset));  // open: Qn, preset
  D_Flip_Flop d_ff_10 (.D(undriven_4), .clk(Split), .Q(M2), .reset(Reset));  // open: Qn, preset
  D_Flip_Flop d_ff_11 (.D(undriven_5), .clk(Split), .Q(M3), .reset(Reset));  // open: Qn, preset
  D_Flip_Flop d_ff_12 (.D(undriven_6), .clk(Split), .Q(MM0), .reset(Reset));  // open: Qn, preset
  D_Flip_Flop d_ff_13 (.D(undriven_7), .clk(Split), .Q(MM1), .reset(Reset));  // open: Qn, preset
  D_Flip_Flop d_ff_14 (.D(undriven_8), .clk(Split), .Q(MM2), .reset(Reset));  // open: Qn, preset
  D_Flip_Flop d_ff_15 (.D(undriven_9), .clk(Split), .Q(MM3), .reset(Reset));  // open: Qn, preset

  // Notes on the sheet:
  //   Stage 4
endmodule
